// Logisim project mother.circ as structural Verilog: 2 circuits, main circuit main
module main (
  input  in_1,
  input  in_2
);

  wire die_1_p1, die_1_p4, die_1_p6, die_1_p7, die_1_p9, die_1_p10, die_1_p15, die_1_p16, die_1_p17,
       die_1_p18, die_1_p19, die_1_p20, on_off_sys_1_clk_out, on_off_sys_1_rst_out;
  wire [7:0] die_1_p5;
  wire [19:0] die_1_p8;
  wire [31:0] die_1_p13, die_1_p14;
  wire [63:0] die_1_p12, rom_bios_1_data_out;

  LED led_1 (.in(die_1_p1));
  On_Off_Sys on_off_sys_1 (.RST(in_2), .Clk(in_1), .RST_Out(on_off_sys_1_rst_out), .Clk_Out(on_off_sys_1_clk_out));
  ROM_BIOS rom_bios_1 (.Addr(die_1_p8), .Data_Out(rom_bios_1_data_out));
  // Die die_1: pin names not known; wires that end beside it: die_1_p1, on_off_sys_1_clk_out, on_off_sys_1_rst_out, die_1_p4, die_1_p5, die_1_p6, die_1_p7, die_1_p8, die_1_p9, die_1_p10, rom_bios_1_data_out, die_1_p12, die_1_p13, die_1_p14, die_1_p15, die_1_p16, die_1_p17, die_1_p18, die_1_p19, die_1_p20
  // Probe on rom_bios_1_data_out
  // Probe on die_1_p8
  Memory memory_1 (
    .Write_En(die_1_p4), .RST(die_1_p10), .Read_En(die_1_p6), .Write_Flags(die_1_p5), .Clk(die_1_p9),
    .Data_In(die_1_p14), .Addr(die_1_p13), .RAM_Ready(die_1_p7), .out_9(die_1_p12));
  // Probe on die_1_p14
  // Probe on die_1_p12
  // Probe on die_1_p13
  // Probe on die_1_p15
  // Probe on die_1_p16
  // Probe on die_1_p17
  // Probe on die_1_p18
  // Probe on die_1_p19
  // Probe on die_1_p20
endmodule

module On_Off_Sys (
  input  RST,
  input  Clk,
  output RST_Out,
  output Clk_Out
);

  wire and_1_out, and_2_out, and_3_out, and_4_out, and_5_out, and_6_out, and_7_out, and_8_out, and_9_out,
       and_10_out, and_11_out, and_12_out, and_13_out, or_1_out, or_2_out, or_3_out, or_4_out, Q0, Q1, Q2;

  and and_1 (and_1_out, ~Q1, RST);  // AND_Gate
  and and_2 (and_2_out, ~Q1, Q0);  // AND_Gate
  and and_3 (and_3_out, Q0, RST);
  and and_4 (and_4_out, ~Q0, Q2);  // AND_Gate
  and and_5 (and_5_out, ~Q2, Q0);  // AND_Gate
  and and_6 (and_6_out, Q1, ~Q0);  // AND_Gate
  and and_7 (and_7_out, Q1, RST);
  and and_8 (and_8_out, Q2, ~Q0);  // AND_Gate
  and and_9 (and_9_out, Q2, RST);
  and and_10 (and_10_out, Q1, ~Q0, RST);  // AND_Gate
  or or_1 (or_1_out, and_1_out, and_2_out, and_3_out, and_4_out);
  or or_2 (or_2_out, and_5_out, and_6_out, and_7_out);
  or or_3 (or_3_out, and_8_out, and_9_out, and_10_out);
  D_Flip_Flop d_ff_1 (.D(or_1_out), .clk(Clk), .Q(Q0));  // open: Qn, preset, reset
  D_Flip_Flop d_ff_2 (.D(or_2_out), .clk(Clk), .Q(Q1));  // open: Qn, preset, reset
  D_Flip_Flop d_ff_3 (.D(or_3_out), .clk(Clk), .Q(Q2));  // open: Qn, preset, reset
  and and_11 (and_11_out, Q2, Q1, ~Q0);  // AND_Gate
  and and_12 (and_12_out, ~Q2, ~Q1, Q0);  // AND_Gate
  or or_4 (or_4_out, Q0, Q1);
  or or_5 (RST_Out, and_11_out, and_12_out);
  and and_13 (and_13_out, ~Q2, or_4_out);  // AND_Gate
  and and_14 (Clk_Out, and_13_out, Clk);
endmodule
